// Logisim project Controllers.circ as structural Verilog: 4 circuits, main circuit ALU Controller Functions
// ALUCF
module ALU_Controller_Functions (
  input  F3,
  input  F2,
  input  F1,
  input  F0,
  output A2,
  output A1,
  output A0,
  output JR
);

  wire and_2_out, not_1_out, not_2_out, not_3_out, not_4_out, not_5_out, not_6_out;

  not not_1 (not_1_out, F1);
  or or_1 (A2, not_1_out, F2);
  and and_1 (A1, F2, not_2_out);
  not not_2 (not_2_out, F1);
  not not_3 (not_3_out, F3);
  and and_2 (and_2_out, not_3_out, F1);
  not not_4 (not_4_out, F2);
  not not_5 (not_5_out, F1);
  not not_6 (not_6_out, F0);
  or or_2 (A0, F0, and_2_out);
  and and_3 (JR, F3, not_4_out, not_5_out, not_6_out);
endmodule

// ALUC
module ALU_Controller (
  input  [1:0] ALU_Op,
  input  [5:0] FUNCT,
  output JR,
  output [2:0] ALU_OP_2
);

  wire [2:0] alu_controller_functions_1_a2;

  ALU_Controller_Functions alu_controller_functions_1 (
    .F3(FUNCT[0]), .F2(FUNCT[1]), .F1(FUNCT[2]), .F0(FUNCT[3]), .A2(alu_controller_functions_1_a2[0]),
    .A1(alu_controller_functions_1_a2[1]), .A0(alu_controller_functions_1_a2[2]), .JR(JR));
  Multiplexer #(.select(2), .width(3)) multiplexer_1 (
    .in0(3'b100), .in1(3'b001), .in2(alu_controller_functions_1_a2), .out(ALU_OP_2), .sel(ALU_Op));  // open: in3, en
endmodule

module Control_Unit_Op (
  input  OP5,
  input  OP4,
  input  OP3,
  input  OP2,
  input  OP1,
  input  OP0,
  output RDOPT1,
  output RDOPT0,
  output JUMPOPT1,
  output JUMPOPT0,
  output MEMREAD,
  output MEMWRITE,
  output WDOPT1,
  output WDOPT0,
  output ALUOP1,
  output ALUOP0,
  output ALUSRC,
  output ENRBWR
);

  wire and_3_out, and_4_out, and_6_out, and_7_out, not_1_out, not_3_out, not_4_out, not_5_out, not_6_out,
       not_7_out, not_8_out, not_9_out, not_10_out, not_11_out;

  not not_1 (not_1_out, OP5);
  not not_2 (RDOPT0, OP1);
  not not_3 (not_3_out, OP1);
  or or_1 (JUMPOPT0, OP0, OP2);
  not not_4 (not_4_out, OP3);
  not not_5 (not_5_out, OP5);
  not not_6 (not_6_out, OP0);
  not not_7 (not_7_out, OP2);
  not not_8 (not_8_out, OP1);
  not not_9 (not_9_out, OP2);
  not not_10 (not_10_out, OP1);
  not not_11 (not_11_out, OP3);
  and and_1 (RDOPT1, not_1_out, OP1);
  or or_2 (JUMPOPT1, not_3_out, OP5);
  and and_2 (MEMREAD, OP5, not_4_out);
  and and_3 (and_3_out, not_5_out, OP1);
  and and_4 (and_4_out, OP1, not_6_out);
  and and_5 (ALUOP1, not_7_out, not_8_out);
  and and_6 (and_6_out, not_9_out, not_10_out);
  and and_7 (and_7_out, not_11_out, OP0);
  or or_3 (WDOPT1, and_3_out, OP2, OP3);
  or or_4 (WDOPT0, and_4_out, OP2, OP5);
  or or_5 (ENRBWR, and_6_out, and_7_out);

  assign ALUOP0 = OP2;
  assign ALUSRC = OP1;
  assign MEMWRITE = OP3;
endmodule

// CU
module Control_Unit (
  input  [5:0] OP,
  output [1:0] RDOPT,
  output [1:0] JUMPOPT,
  output MEMREAD,
  output MEMWRITE,
  output [1:0] WDPOPT,
  output [1:0] ALUPOP,
  output ALUSRC,
  output ENRBWR
);

  Control_Unit_Op control_unit_op_1 (
    .OP5(OP[5]), .OP4(OP[4]), .OP3(OP[3]), .OP2(OP[2]), .OP1(OP[1]), .OP0(OP[0]), .RDOPT1(RDOPT[1]),
    .RDOPT0(RDOPT[0]), .JUMPOPT1(JUMPOPT[1]), .JUMPOPT0(JUMPOPT[0]), .MEMREAD(MEMREAD), .MEMWRITE(MEMWRITE),
    .WDOPT1(WDPOPT[1]), .WDOPT0(WDPOPT[0]), .ALUOP1(ALUPOP[1]), .ALUOP0(ALUPOP[0]), .ALUSRC(ALUSRC),
    .ENRBWR(ENRBWR));
endmodule
