// Logisim project Unicycle Processor.circ as structural Verilog: 1 circuit, main circuit Processor
module Processor (
  input  in_1
);

  wire alu_thirty_two_bits_1_zero, ALUSRC, and_1_out, and_2_out, CLK, control_unit_1_enrbwr, JR, MEMREAD,
       MEMWRITE, not_1_out;
  wire [1:0] ALUOP, JUMPOPT, RDOPT, WDOPT;
  wire [2:0] ALU_OP;
  wire [4:0] multiplexer_1_out;
  wire [27:0] shifter_1_out;
  wire [31:0] adder_1_out, adder_3_out, ALURESULT, DMDATA, INM, Inst, multiplexer_3_out, multiplexer_4_out,
       multiplexer_5_out, PC_8, PC_q, PCRESULT, register_bank_1_r1_2, shifter_2_out, WD, WDR;

  Register #(.width(32)) PC (.D(PCRESULT), .Q(PC_q), .clk(CLK), .clr(in_1));  // open: en
  Adder #(.width(32)) adder_1 (.a(32'h4), .b(PC_q), .out(adder_1_out));  // open: cin, cout
  Instruction_Memory instruction_memory_1 (.PC_DIR(PC_q), .INSTRUCTION(Inst));
  Adder #(.width(32)) adder_2 (.a(PC_q), .b(32'h8), .out(PC_8));  // open: cin, cout
  Shifter #(.width(28)) shifter_1 (.in(Inst[27:0]), .\dist (5'b00010), .out(shifter_1_out));
  Control_Unit control_unit_1 (
    .OP(Inst[31:26]), .RDOPT(RDOPT), .JUMPOPT(JUMPOPT), .MEMREAD(MEMREAD), .MEMWRITE(MEMWRITE),
    .WDPOPT(WDOPT), .ALUPOP(ALUOP), .ALUSRC(ALUSRC), .ENRBWR(control_unit_1_enrbwr));
  not not_1 (not_1_out, JR);
  and and_1 (and_1_out, control_unit_1_enrbwr, not_1_out);
  Multiplexer #(.select(2), .width(5)) multiplexer_1 (
    .in0(Inst[20:16]), .in1(Inst[15:11]), .in2({5{1'b1}}), .in3({5{1'b0}}), .out(multiplexer_1_out),
    .sel(RDOPT));  // open: en
  Multiplexer #(.select(2), .width(32)) multiplexer_2 (
    .in0(ALURESULT), .in1(DMDATA), .in2(PC_8), .in3({32{1'b0}}), .out(WDR), .sel(WDOPT));  // open: en
  Register_Bank register_bank_1 (
    .Clk(CLK), .R1(Inst[25:21]), .R2(Inst[20:16]), .WR(multiplexer_1_out), .WD(WDR), .ENWR(and_1_out),
    .R1_2(register_bank_1_r1_2), .R2_2(WD));
  assign INM = {{16{Inst[15]}}, Inst[15:0]};  // Bit_Extender bit_extender_1
  Clock clock_1 (.out(CLK));
  Shifter #(.width(32)) shifter_2 (.in(INM), .\dist (5'b00010), .out(shifter_2_out));
  Multiplexer #(.width(32)) multiplexer_3 (.in0(WD), .in1(INM), .out(multiplexer_3_out), .sel(ALUSRC));  // open: en
  ALU_Controller alu_controller_1 (.ALU_Op(ALUOP), .FUNCT(Inst[5:0]), .JR(JR), .ALU_OP_2(ALU_OP));
  Adder #(.width(32)) adder_3 (.a(adder_1_out), .b(shifter_2_out), .out(adder_3_out));  // open: cin, cout
  and and_2 (and_2_out, JUMPOPT[0], JUMPOPT[1], alu_thirty_two_bits_1_zero);
  ALU_Thirty_Two_Bits alu_thirty_two_bits_1 (
    .RESULT(ALURESULT), .ALU_CODE(ALU_OP), .R2(multiplexer_3_out), .CIN(1'b0), .R1(register_bank_1_r1_2),
    .ZERO(alu_thirty_two_bits_1_zero));
  Multiplexer #(.width(32)) multiplexer_4 (
    .in0(adder_1_out), .in1(register_bank_1_r1_2), .out(multiplexer_4_out), .sel(JR));  // open: en
  Multiplexer #(.width(32)) multiplexer_5 (
    .in0(adder_1_out), .in1(adder_3_out), .out(multiplexer_5_out), .sel(and_2_out));  // open: en
  // Data_Memory data_memory_1: pin names not known; wires that end beside it: ALURESULT, CLK, WD, MEMREAD, MEMWRITE, DMDATA
  // Probe on PCRESULT
  // Probe on Inst
  // Probe on DMDATA
  // Probe on WDR
  // Probe on WD
  Multiplexer #(.select(2), .width(32)) multiplexer_6 (
    .in0({adder_1_out[31:28], shifter_1_out}), .in1({adder_1_out[31:28], shifter_1_out}),
    .in2(multiplexer_4_out), .in3(multiplexer_5_out), .out(PCRESULT), .sel(JUMPOPT));  // open: en
  // Probe on ALU_OP
  // Probe on RDOPT
  // Probe on WDOPT
  // Probe on INM
  // Probe on JUMPOPT
  // Probe on ALURESULT
endmodule
